# Fritzing sketch external-led-pot-toggle (saved by Fritzing 0.9.3b)
breadboards: 1

parts:
  Part1 = Arduino Uno (Rev3)
  LED1 = smd LED [color="Red (633nm)" package="0603 [SMD]"]
  R1 = Resistor [tolerance=±5% resistance=10k package="2512 [SMD]"]
  R2 = TRIMPOT [package=3362u-2]
  R3 = Resistor [tolerance=±5% resistance=10k package="2512 [SMD]"]
  S1 = Toggle Switch [package=THT]
  R4 = Resistor [tolerance=±5% resistance=10k package="2512 [SMD]"]

nets:
  N1: Part1.A0, R2.WIPER
  N2: Part1.D13/SCK, LED1.cathode
  N3: Part1.D7, S1.COM
  N4: Part1.3V3, R1.Pin_1
  N5: Part1.GND, R2.CW, S1.L2
  N6: LED1.anode, R1.Pin_0
  N7: R2.CCW, R3.Pin_0
  N8: S1.L1, R4.Pin_0
